# Fritzing sketch Skull (saved by Fritzing 0.8.3b)
breadboards: 1

parts:
  Part1 = Arduino Uno (Rev3)
  LED1 = LED - 5mm [color="Red (633nm)" package="5 mm [THT]"]
  LED2 = LED - 5mm [color="Red (633nm)" package="5 mm [THT]"]
  LED3 = LED - 5mm [color="White (4500K)" package="5 mm [THT]"]
  LED4 = LED - 5mm [color="White (4500K)" package="5 mm [THT]"]
  R1 = Resistor [tolerance=±5% resistance=220 package=THT]
  R5 = Resistor [tolerance=±5% resistance=220 package=THT]
  R6 = Resistor [tolerance=±5% resistance=220 package=THT]
  R7 = Resistor [tolerance=±5% resistance=220 package=THT]

nets:
  N1: Part1.A0, LED1.anode
  N2: Part1.A1, LED4.anode
  N3: Part1.A2, LED3.anode
  N4: Part1.A3, LED2.anode
  N5: Part1.GND, R1.Pin_0, R5.Pin_0, R6.Pin_0, R7.Pin_0
  N6: LED1.cathode, R1.Pin_1
  N7: LED2.cathode, R7.Pin_1
  N8: LED3.cathode, R6.Pin_1
  N9: LED4.cathode, R5.Pin_1
